// Logisim project CS23I1001-DSD_LAB.circ as structural Verilog: 3 circuits, main circuit main
module main (
  input  in_1,
  input  in_2,
  input  in_3,
  input  in_4,
  input  in_5,
  input  in_6,
  input  in_7,
  input  in_8,
  input  in_9,
  input  in_10,
  input  Stop_Switch,
  input  in_12,
  input  in_13,
  input  in_14
);

  wire and_1_out, and_2_out, and_3_out, and_4_out, and_5_out, and_6_out, and_7_out, and_8_out, and_9_out,
       and_10_out, and_11_out, and_12_out, and_13_out, and_14_out, clock_1_out, clock_2_out, not_1_out,
       not_2_out, not_3_out, not_4_out, not_5_out, or_1_out, t_ff_1_qn, t_ff_2_qn, t_ff_3_qn, t_ff_4_qn;
  wire [2:0] t_ff_1_q, t_ff_2_q;
  wire [3:0] j_k_ff_1_q, j_k_ff_2_q;

  not not_1 (not_1_out, in_1);
  Clock clock_1 (.out(clock_1_out));
  Clock clock_2 (.out(clock_2_out));
  and and_1 (and_1_out, not_1_out, clock_1_out);
  J_K_Flip_Flop j_k_ff_1 (
    .J(or_1_out), .K(or_1_out), .clk(and_1_out), .Q(j_k_ff_1_q[0]), .preset(in_6), .reset(in_7));  // open: Qn
  and and_2 (and_2_out, clock_2_out, not_2_out);
  not not_2 (not_2_out, Stop_Switch);
  T_Flip_Flop t_ff_1 (.T(in_4), .clk(and_1_out), .Q(t_ff_1_q[0]), .Qn(t_ff_1_qn), .reset(in_5), .preset(in_2));
  T_Flip_Flop t_ff_2 (.T(in_10), .clk(and_2_out), .Q(t_ff_2_q[0]), .Qn(t_ff_2_qn), .reset(in_12), .preset(in_8));
  J_K_Flip_Flop j_k_ff_2 (
    .J(and_11_out), .K(and_11_out), .clk(and_2_out), .Q(j_k_ff_2_q[0]), .preset(in_13), .reset(in_14));  // open: Qn
  and and_3 (and_3_out, j_k_ff_1_q[0], or_1_out);
  J_K_Flip_Flop j_k_ff_3 (
    .J(and_3_out), .K(and_3_out), .clk(and_1_out), .Q(j_k_ff_1_q[1]), .preset(in_6), .reset(in_7));  // open: Qn
  and and_4 (and_4_out, j_k_ff_2_q[0], and_11_out);
  T_Flip_Flop t_ff_3 (.T(t_ff_1_qn), .clk(and_1_out), .Q(t_ff_1_q[1]), .Qn(t_ff_3_qn), .reset(in_5), .preset(in_2));
  T_Flip_Flop t_ff_4 (.T(t_ff_2_qn), .clk(and_2_out), .Q(t_ff_2_q[1]), .Qn(t_ff_4_qn), .reset(in_12), .preset(in_8));
  J_K_Flip_Flop j_k_ff_4 (
    .J(and_4_out), .K(and_4_out), .clk(and_2_out), .Q(j_k_ff_2_q[1]), .preset(in_13), .reset(in_14));  // open: Qn
  or or_1 (or_1_out, and_9_out, and_13_out);
  and and_5 (and_5_out, j_k_ff_1_q[1], and_3_out);
  and and_6 (and_6_out, t_ff_3_qn, t_ff_1_qn);
  J_K_Flip_Flop j_k_ff_5 (
    .J(and_5_out), .K(and_5_out), .clk(and_1_out), .Q(j_k_ff_1_q[2]), .preset(in_6), .reset(in_7));  // open: Qn
  and and_7 (and_7_out, t_ff_4_qn, t_ff_2_qn);
  and and_8 (and_8_out, j_k_ff_2_q[1], and_4_out);
  T_Flip_Flop t_ff_5 (.T(and_6_out), .clk(and_1_out), .Q(t_ff_1_q[2]), .reset(in_5), .preset(in_2));  // open: Qn
  and and_9 (and_9_out, t_ff_1_q[2], not_3_out, not_4_out);
  T_Flip_Flop t_ff_6 (.T(and_7_out), .clk(and_2_out), .Q(t_ff_2_q[2]), .reset(in_12), .preset(in_8));  // open: Qn
  J_K_Flip_Flop j_k_ff_6 (
    .J(and_8_out), .K(and_8_out), .clk(and_2_out), .Q(j_k_ff_2_q[2]), .preset(in_13), .reset(in_14));  // open: Qn
  not not_3 (not_3_out, t_ff_1_q[1]);
  not not_4 (not_4_out, t_ff_1_q[0]);
  and and_10 (and_10_out, j_k_ff_1_q[2], and_5_out);
  and and_11 (and_11_out, and_14_out, in_10);
  and and_12 (and_12_out, j_k_ff_2_q[2], and_8_out);
  Hex_Digit_Display hex_digit_display_1 (.value({in_3, t_ff_1_q}));  // open: dp
  J_K_Flip_Flop j_k_ff_7 (
    .J(and_10_out), .K(and_10_out), .clk(and_1_out), .Q(j_k_ff_1_q[3]), .preset(in_6), .reset(in_7));  // open: Qn
  not not_5 (not_5_out, t_ff_2_q[1]);
  J_K_Flip_Flop j_k_ff_8 (
    .J(and_12_out), .K(and_12_out), .clk(and_2_out), .Q(j_k_ff_2_q[3]), .preset(in_13), .reset(in_14));  // open: Qn
  and and_13 (and_13_out, t_ff_1_q[2], t_ff_1_q[1], t_ff_1_q[0]);
  Hex_Digit_Display hex_digit_display_2 (.value({in_9, t_ff_2_q}));  // open: dp
  and and_14 (and_14_out, t_ff_2_q[2], not_5_out, t_ff_2_q[0]);
  Hex_Digit_Display hex_digit_display_3 (.value(j_k_ff_1_q));  // open: dp
  Hex_Digit_Display hex_digit_display_4 (.value(j_k_ff_2_q));  // open: dp

  // Notes on the sheet:
  //   in_4: initial=0x1
  //   in_10: initial=0x1
  //   Stop Switch
  //   Count Seven and Four in a Cycle
  //   Number of Fives in  Cycles
  //   Down Counter
  //   Down Counter
  //   Number of Fives
  //   Number of Seven and Fours
endmodule

module sevenandfour (
  input  in_1,
  input  in_2,
  input  in_3,
  input  in_4,
  input  in_5,
  input  in_6,
  input  in_7,
  input  in_8
);

  wire and_1_out, and_2_out, and_3_out, and_4_out, and_5_out, and_6_out, and_7_out, clock_1_out, not_1_out,
       not_2_out, not_3_out, or_1_out, t_ff_1_qn, t_ff_2_qn;
  wire [2:0] t_ff_1_q;
  wire [3:0] j_k_ff_1_q;

  not not_1 (not_1_out, in_1);
  Clock clock_1 (.out(clock_1_out));
  and and_1 (and_1_out, not_1_out, clock_1_out);
  J_K_Flip_Flop j_k_ff_1 (.J(or_1_out), .K(or_1_out), .clk(and_1_out), .Q(j_k_ff_1_q[0]));  // open: Qn, preset, reset
  T_Flip_Flop t_ff_1 (.T(in_6), .clk(and_1_out), .Q(t_ff_1_q[0]), .Qn(t_ff_1_qn), .reset(in_8), .preset(in_3));
  and and_2 (and_2_out, j_k_ff_1_q[0], or_1_out);
  J_K_Flip_Flop j_k_ff_2 (.J(and_2_out), .K(and_2_out), .clk(and_1_out), .Q(j_k_ff_1_q[1]));  // open: Qn, preset, reset
  T_Flip_Flop t_ff_2 (.T(t_ff_1_qn), .clk(and_1_out), .Q(t_ff_1_q[1]), .Qn(t_ff_2_qn), .reset(in_7), .preset(in_4));
  or or_1 (or_1_out, and_5_out, and_7_out);
  and and_3 (and_3_out, j_k_ff_1_q[1], and_2_out);
  and and_4 (and_4_out, t_ff_2_qn, t_ff_1_qn);
  J_K_Flip_Flop j_k_ff_3 (.J(and_3_out), .K(and_3_out), .clk(and_1_out), .Q(j_k_ff_1_q[2]));  // open: Qn, preset, reset
  T_Flip_Flop t_ff_3 (.T(and_4_out), .clk(and_1_out), .Q(t_ff_1_q[2]), .preset(in_2));  // open: Qn, reset
  and and_5 (and_5_out, t_ff_1_q[2], not_2_out, not_3_out);
  not not_2 (not_2_out, t_ff_1_q[1]);
  not not_3 (not_3_out, t_ff_1_q[0]);
  and and_6 (and_6_out, j_k_ff_1_q[2], and_3_out);
  Hex_Digit_Display hex_digit_display_1 (.value({in_5, t_ff_1_q}));  // open: dp
  J_K_Flip_Flop j_k_ff_4 (.J(and_6_out), .K(and_6_out), .clk(and_1_out), .Q(j_k_ff_1_q[3]));  // open: Qn, preset, reset
  and and_7 (and_7_out, t_ff_1_q[2], t_ff_1_q[1], t_ff_1_q[0]);
  Hex_Digit_Display hex_digit_display_2 (.value(j_k_ff_1_q));  // open: dp

  // Notes on the sheet:
  //   in_6: initial=0x1
  //   Stop Switch
  //   Count Seven and Four in a Cycle
  //   Down Counter
  //   Number of Seven and Fours
endmodule

module fivecount (
  input  in_1,
  input  in_2,
  input  in_3,
  input  in_4,
  input  in_5,
  input  in_6,
  input  in_7,
  input  Stop_Switch
);

  wire and_1_out, and_2_out, and_3_out, and_4_out, and_5_out, and_6_out, and_7_out, clock_1_out, not_1_out,
       not_2_out, t_ff_1_qn, t_ff_2_qn;
  wire [2:0] t_ff_1_q;
  wire [3:0] j_k_ff_1_q;

  Clock clock_1 (.out(clock_1_out));
  and and_1 (and_1_out, clock_1_out, not_1_out);
  not not_1 (not_1_out, Stop_Switch);
  J_K_Flip_Flop j_k_ff_1 (.J(and_5_out), .K(and_5_out), .clk(and_1_out), .Q(j_k_ff_1_q[0]));  // open: Qn, preset, reset
  T_Flip_Flop t_ff_1 (.T(in_5), .clk(and_1_out), .Q(t_ff_1_q[0]), .Qn(t_ff_1_qn), .reset(in_7), .preset(in_2));
  and and_2 (and_2_out, j_k_ff_1_q[0], and_5_out);
  T_Flip_Flop t_ff_2 (.T(t_ff_1_qn), .clk(and_1_out), .Q(t_ff_1_q[1]), .Qn(t_ff_2_qn), .reset(in_6), .preset(in_3));
  J_K_Flip_Flop j_k_ff_2 (.J(and_2_out), .K(and_2_out), .clk(and_1_out), .Q(j_k_ff_1_q[1]));  // open: Qn, preset, reset
  and and_3 (and_3_out, t_ff_2_qn, t_ff_1_qn);
  and and_4 (and_4_out, j_k_ff_1_q[1], and_2_out);
  T_Flip_Flop t_ff_3 (.T(and_3_out), .clk(and_1_out), .Q(t_ff_1_q[2]), .preset(in_1));  // open: Qn, reset
  J_K_Flip_Flop j_k_ff_3 (.J(and_4_out), .K(and_4_out), .clk(and_1_out), .Q(j_k_ff_1_q[2]));  // open: Qn, preset, reset
  and and_5 (and_5_out, and_7_out, in_5);
  and and_6 (and_6_out, j_k_ff_1_q[2], and_4_out);
  not not_2 (not_2_out, t_ff_1_q[1]);
  J_K_Flip_Flop j_k_ff_4 (.J(and_6_out), .K(and_6_out), .clk(and_1_out), .Q(j_k_ff_1_q[3]));  // open: Qn, preset, reset
  Hex_Digit_Display hex_digit_display_1 (.value({in_4, t_ff_1_q}));  // open: dp
  and and_7 (and_7_out, t_ff_1_q[2], not_2_out, t_ff_1_q[0]);
  Hex_Digit_Display hex_digit_display_2 (.value(j_k_ff_1_q));  // open: dp

  // Notes on the sheet:
  //   in_5: initial=0x1
  //   Number of Fives in  Cycles
  //   Down Counter
  //   Number of Fives
endmodule
